# Fritzing sketch schema_led (saved by Fritzing 0.9.2b)
breadboards: 1

parts:
  R1 = Resistor [tolerance=±5% resistance=100 package=THT]
  LED1 = LED - 5mm [color="Yellow (592nm)" package="5 mm [THT]"]
  Raspberry_Pi1 = Raspberry Pi 2

nets:
  N1: R1.Pin_0, LED1.cathode
  N2: R1.Pin_1, Raspberry_Pi1.GND
  N3: LED1.anode, Raspberry_Pi1.GPIO21
